# Fritzing sketch PCB[FritzingSketch] (saved by Fritzing 0.9.3b)
breadboards: 1

parts:
  Part1 = Arduino Uno (Rev3) - ICSP
  U1 = Optocoupler [package=THT]
  D1 = Rectifier Diode [part_number=1N4001 package="300 mil [THT]"]
  R1 = Resistor [tolerance=±5% resistance=220 package=THT]
  MIDI_In = MIDI_CONN_FEMALE [package=din_5_female]
  StartStop = AUDIO-JACK2 [package=audio-jack]
  Clock = AUDIO-JACK2 [package=audio-jack]
  Write = AUDIO-JACK2 [package=audio-jack]
  R2 = Resistor [tolerance=±5% resistance=1k package=THT]
  Trigger_Button = SWITCH-MOMENTARY-2 [package=tactile-pth-12mm]
  R3 = Resistor [tolerance=±5% resistance=10k package=THT]

nets:
  N1: Part1.GND, U1.Pin_4, StartStop.SLEEVE, Clock.SLEEVE, Write.SLEEVE, R3.Pin_1
  N2: Part1.D0/RX, U1.Pin_5, R2.Pin_1
  N3: Part1.D3_PWM, Trigger_Button.1, R3.Pin_0
  N4: Part1.D5_PWM, StartStop.TIP
  N5: Part1.D6_PWM, Clock.TIP
  N6: Part1.D7, Write.TIP
  N7: Part1.5V, R2.Pin_0, Trigger_Button.2
  N8: U1.Pin_1, D1.cathode, R1.Pin_1
  N9: U1.Pin_2, D1.anode, MIDI_In.MIDI_IN
  N10: R1.Pin_0, MIDI_In.MIDI_OUT
